# Fritzing sketch talking_clock (saved by Fritzing 1.0.6)
breadboards: 1

parts:
  Announce = Pushbutton [package="[SMD]"]
  Plus = Pushbutton [package="[SMD]"]
  Minus = Pushbutton [package="[SMD]"]
  microSD1 = MicroSD Card Module
  Part2 = Adafruit MAX98357A I2S 3W Class D Amplifier [part_number="Adafruit #3006"]
  Mod1 = Raspberry Pi Pico
  Reset = Pushbutton [package="[SMD]"]
  ZS-042_RTC1 = ZS-042 RTC Module
  Part1 = RTC DS3231  # not connected

nets:
  N1: Announce.Pin_1, Announce.Pin_2, Mod1.pin_9
  GND: Announce.Pin_3, Announce.Pin_4, Plus.Pin_3, Plus.Pin_4, Minus.Pin_3, Minus.Pin_4, microSD1.GND, Part2.GND, Mod1.pin_3, Mod1.pin_8, Mod1.pin_13, Mod1.pin_18, Mod1.pin_23, Mod1.pin_28, Mod1.pin_33, Mod1.pin_38, Mod1.pin_42, Reset.Pin_3, Reset.Pin_4, ZS-042_RTC1.GND
  N2: Plus.Pin_1, Plus.Pin_2, Mod1.pin_10
  N3: Minus.Pin_1, Minus.Pin_2, Mod1.pin_11
  VCC: microSD1.VCC, Part2.VIN, Mod1.pin_40, ZS-042_RTC1.VCC
  N4: microSD1.MISO, Mod1.pin_21
  N5: microSD1.MOSI, Mod1.pin_25
  N6: microSD1.SCK, Mod1.pin_24
  N7: microSD1.CS, Mod1.pin_22
  N8: Part2.SD_MODE, Mod1.pin_12
  N9: Part2.GAIN, Mod1.pin_17
  N10: Part2.DIN, Mod1.pin_14
  N11: Part2.BCLK, Mod1.pin_15
  N12: Part2.LRCLK, Mod1.pin_16
  N13: Mod1.pin_1, ZS-042_RTC1.SCL
  N14: Mod1.pin_2, ZS-042_RTC1.SDA
  N15: Mod1.pin_30, Reset.Pin_1, Reset.Pin_2

custom parts:
  Adafruit MAX98357A I2S 3W Class D Amplifier: Listen to this good news - we now have an all in one digital audio amp breakout board that works incredibly well with the Raspberry Pi! If you're looking for an easy and low cost way to get you digital sound files bumpin' then the MAX08357 I2S Amp Breakout is for you. It takes standard I2S digital audio input and, not only decodes it into analog, but also amplifies it directly into a speaker.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
  Raspberry Pi Pico: Raspberry Pi Pico. Based around the RP2040 microcontroller the Pico is a low cost microcontroller device bringing Raspberry Pi quality, cost, and easy of use to the microcontroller space. Jan 2021, Split part in to two versions: tht (this one) and SMD. This one will drill holes for a .1 in header in pcb to allow plugging in the module as well as providing pads to solder the module to the top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
  RTC DS3231: DS3231 with akku
